// Digital circuit ALU.dig as structural Verilog
module ALU (
  input  [7:0] DataIn,
  input  Clk,
  input  InA,
  input  InB,
  input  Mode,
  output [7:0] OutA,
  output [7:0] OutB,
  output [7:0] Q
);

  wire [2:0] Mode_q;
  wire [7:0] add_1_s;

  Register #(.Bits(8)) A (.D(DataIn), .C(Clk), .en(InA), .Q(OutA));
  Register #(.Bits(8)) B (.D(DataIn), .C(Clk), .en(InB), .Q(OutB));
  Register #(.Bits(3)) u_Mode (.D(DataIn[2:0]), .C(Clk), .en(Mode), .Q(Mode_q));
  Add #(.Bits(8)) add_1 (.a(OutA), .b(OutB), .c_i(1'b0), .s(add_1_s));  // open: c_o
  Multiplexer #(.Bits(8), .Selector_Bits(3)) multiplexer_1 (
    .sel(Mode_q), .in_0(add_1_s), .in_1({8{1'b0}}), .in_2({8{1'b0}}), .in_3({8{1'b0}}), .in_4({8{1'b0}}),
    .in_5({8{1'b0}}), .in_6({8{1'b0}}), .in_7({8{1'b0}}), .out(Q));
endmodule
